// Digital circuit ALU.dig as structural Verilog
module ALU (
  input  [3:0] operation,
  input  [31:0] src1,
  input  [31:0] src2,
  output [31:0] Result,
  output [31:0] Zero,
  output [31:0] Overflow,
  output CarryOut
);

  wire ADDER_c_o, SUBSTRACTOR_c_o;
  wire [31:0] ADDER_s, SLL_out, SUBSTRACTOR_s;

  BarrelShifter #(.Bits(32)) SLL (.in(src1), .shift(src2[5:0]), .out(SLL_out));
  Add #(.Bits(32)) ADDER (.a(src1), .b(src2), .c_i(1'b0), .s(ADDER_s), .c_o(ADDER_c_o));
  Sub #(.Bits(32)) SUBSTRACTOR (.a(src1), .b(src2), .c_i(1'b0), .s(SUBSTRACTOR_s), .c_o(SUBSTRACTOR_c_o));
  Multiplexer #(.Selector_Bits(4), .Bits(32)) multiplexer_1 (
    .sel(operation), .in_0(ADDER_s), .in_1(SLL_out), .in_2(ADDER_s), .in_3({32{1'b0}}), .in_4({32{1'b0}}),
    .in_5({32{1'b0}}), .in_6({32{1'b0}}), .in_7({32{1'b0}}), .in_8(SUBSTRACTOR_s), .in_9({32{1'b0}}),
    .in_10({32{1'b0}}), .in_11({32{1'b0}}), .in_12({32{1'b0}}), .in_13({32{1'b0}}), .in_14({32{1'b0}}),
    .in_15({32{1'b0}}), .out(Overflow));
  Multiplexer #(.Selector_Bits(4)) multiplexer_2 (
    .sel(operation), .in_0(ADDER_c_o), .in_1(1'b0), .in_2(1'b0), .in_3(1'b0), .in_4(1'b0), .in_5(1'b0),
    .in_6(1'b0), .in_7(1'b0), .in_8(SUBSTRACTOR_c_o), .in_9(1'b0), .in_10(1'b0), .in_11(1'b0), .in_12(1'b0),
    .in_13(1'b0), .in_14(1'b0), .in_15(1'b0), .out(CarryOut));

  assign Result = Overflow;
  assign Zero = Overflow;

  // Notes on the sheet:
  //   Sum
  //   Carry out
endmodule
