// Digital circuit riscv_version3.dig as structural Verilog
module riscv_version3 (
  input  [31:0] _0_32,
  input  [31:0] in_4,
  input  [31:0] _0_33,
  output out_1,
  output [31:0] out_3,
  output [31:0] out_5,
  output [3:0] out_6,
  output [31:0] out_7,
  output [3:0] out_8,
  output [23:0] out_9
);

  wire ALUSrc, Clock, CONTROL_BLOCK_memread, CONTROL_BLOCK_memwrite, CONTROL_BLOCK_regwrite, MemToReg;
  wire [1:0] CONTROL_BLOCK_aluop;
  wire [4:0] CONTROL_BLOCK_rd_inst_11_7, CONTROL_BLOCK_rs1_inst_19_15, CONTROL_BLOCK_rs2_inst_24_20;
  wire [23:0] PC_out;
  wire [31:0] CONTROL_BLOCK_inst_31_0, IMMEDIATE_GENERATION_immidiate, multiplexer_1_out, multiplexer_3_out,
       PROGRAM_MEMORY_d, REGISTER_FILE___only_r0_r8_done_read_data1,
       REGISTER_FILE___only_r0_r8_done_read_data2;

  Counter #(.Bits(24)) PC (.en(1'b1), .C(Clock), .clr(1'b0), .out(PC_out), .ovf(out_1));
  ROM #(.AddrBits(24), .isProgramMemory("true"), .Bits(32)) PROGRAM_MEMORY (
    .A(PC_out), .sel(1'b1), .D(PROGRAM_MEMORY_d));
  InstructionDecoder CONTROL_BLOCK (
    .inst(PROGRAM_MEMORY_d), .rd_inst_11_7(CONTROL_BLOCK_rd_inst_11_7),
    .rs1_inst_19_15(CONTROL_BLOCK_rs1_inst_19_15), .rs2_inst_24_20(CONTROL_BLOCK_rs2_inst_24_20),
    .inst_31_0({CONTROL_BLOCK_inst_31_0[31], out_6[3], CONTROL_BLOCK_inst_31_0[29:15], out_6[2:0], CONTROL_BLOCK_inst_31_0[11:0]}),
    .MemRead(CONTROL_BLOCK_memread), .MemToReg(MemToReg), .ALUOp(CONTROL_BLOCK_aluop),
    .MemWrite(CONTROL_BLOCK_memwrite), .ALUSrc(ALUSrc), .RegWrite(CONTROL_BLOCK_regwrite));  // open: opcode_6_0, func7, funct3, imm, Branch
  RegisterFile REGISTER_FILE___only_r0_r8_done (
    .write_data(multiplexer_3_out), ._0(_0_32), .tmp1(_0_32), .rd_inst_11_7(CONTROL_BLOCK_rd_inst_11_7),
    .rs1_inst_19_15(CONTROL_BLOCK_rs1_inst_19_15), .rs2_inst_24_20(CONTROL_BLOCK_rs2_inst_24_20),
    .tmp2(_0_32), .clk(Clock), .RegWrite(CONTROL_BLOCK_regwrite), ._0_32(_0_33),
    .Read_Data1(REGISTER_FILE___only_r0_r8_done_read_data1),
    .Read_Data2(REGISTER_FILE___only_r0_r8_done_read_data2));
  ImmediateGen IMMEDIATE_GENERATION (
    .instr({CONTROL_BLOCK_inst_31_0[31], out_6[3], CONTROL_BLOCK_inst_31_0[29:15], out_6[2:0], CONTROL_BLOCK_inst_31_0[11:0]}),
    .immidiate(IMMEDIATE_GENERATION_immidiate));
  Button button_1 (.out(Clock));
  Alu_Control_Unit ALU_CONTROL_UNIT (.Control_in(out_6), .Alu_op(CONTROL_BLOCK_aluop), .Operation(out_8));
  Multiplexer #(.Bits(32)) multiplexer_1 (
    .sel(ALUSrc), .in_0(REGISTER_FILE___only_r0_r8_done_read_data2), .in_1(IMMEDIATE_GENERATION_immidiate),
    .out(multiplexer_1_out));
  BarrelShifter #(.Bits(32), .barrelSigned("true")) ShiftLeft1 (
    .in(IMMEDIATE_GENERATION_immidiate), .shift(7'b0000001), .out(out_5));
  ALU ALU (
    .operation(out_8), .src1(REGISTER_FILE___only_r0_r8_done_read_data1), .src2(multiplexer_1_out),
    .Result(out_7));  // open: Zero, Overflow, CarryOut
  Multiplexer #(.Bits(32)) multiplexer_2 (.sel(1'b0), .in_0(in_4), .in_1(out_5));  // open: out
  EEPROMDualPort #(.AddrBits(24), .Bits(32)) MAIN_MEMORY (
    .A(out_7[23:0]), .Din(REGISTER_FILE___only_r0_r8_done_read_data2), .str(CONTROL_BLOCK_memwrite),
    .C(Clock), .ld(CONTROL_BLOCK_memread), .D(out_3));
  Multiplexer #(.Bits(32)) multiplexer_3 (.sel(MemToReg), .in_0(out_7), .in_1(out_3), .out(multiplexer_3_out));

  assign out_9 = out_7[23:0];

  // Notes on the sheet:
  //   0.lw x1,0(x0)
  //      1. lw x2,1(x0)
  //       2.add x3, x1, x2
  //       3.sw x3, 2 (x0) 
  //   4.add x1, x1, x0
  //      5. sub x4, x2, x1
  //       6.sw x4, 3(x0)
  //       7.add x1, x1, x0
  //       8.lw x1, 9(x0)
  //       9.lw x2, 10(x0)
  //       10.sll x3, x1, x2
  //       11.sw x3, 8(x0)
  //   contents of PROGRAM_MEMORY (hex, n*v repeats v):
  //   2083,102103,2081b3,302123,80b3,40110233,4021a3,80b3,902083,a02103
  //   ,2091b3,302423
  //   RISC-V 32bit CPU
  //   Working now: ADD, SUB, SW, LW
  //   contents of MAIN_MEMORY (hex, n*v repeats v):
  //   22,36,7*0,9,2
endmodule
